# Fritzing sketch Untitled Sketch 8 (saved by Fritzing 0.9.4)
circuit board: 8.46667cm x 5.64444cm

parts:
  M1 = DOIT Esp32 DevKit v1 (30 pins long, 11 pins width) [part_number=ESP32S-PIN30]
  Componente1 = InvenSense MPU6050
  M2 = INA219 DC Current Monitor Module [part_number=CJMCU]
  TP1 = TP4056 [chip_label=TP4056 package="DIP (Dual Inline) [THT]"]
  U3 = Mini-360 DC-DC Buck converter [package=THT]
  U4 = Mini-360 DC-DC Buck converter [package=THT]
  C1 = Electrolytic Capacitor [capacitance=100μF package="0807 [SMD, electrolytic]"]
  U5 = SWITCH_SPDT [package=kps-1290]
  J1 = Dagu DGServo 9g header (male) [package=THT]
  J2 = Dagu DGServo 9g header (male) [package=THT]
  J3 = Dagu DGServo 9g header (male) [package=THT]
  J4 = Dagu DGServo 9g header (male) [package=THT]
  J5 = Dagu DGServo 9g header (male) [package=THT]
  J6 = Dagu DGServo 9g header (male) [package=THT]
  J7 = Dagu DGServo 9g header (male) [package=THT]
  J8 = Dagu DGServo 9g header (male) [package=THT]
  J9 = Dagu DGServo 9g header (male) [package=THT]
  J10 = Dagu DGServo 9g header (male) [package=THT]
  J11 = Dagu DGServo 9g header (male) [package=THT]
  J12 = Dagu DGServo 9g header (male) [package=THT]
  U2 = Mini-360 DC-DC Buck converter [package=THT]
  VCC1 = Battery

nets:
  VCC: M1.3V3, Componente1.VCC, M2.VCC
  GND: M1.GND, Componente1.GND, M2.GND, U3.OUT-, C1.-
  N1: M1.D15, J3.pulse
  N2: M1.D2, J2.pulse
  N3: M1.D4, J1.pulse
  N4: M1.D5, J10.pulse
  N5: M1.D18, J7.pulse
  N6: M1.D19, J11.pulse
  N7: M1.D21, J9.pulse
  N8: M1.D22, J8.pulse
  N9: M1.D23, J12.pulse
  N10: M1.D26, Componente1.SCL, M2.SCL
  N11: M1.D27, Componente1.SDA, M2.SDA
  N12: M1.D14, J4.pulse
  N13: M1.D12, J6.pulse
  N14: M1.D13, J5.pulse
  N15: M1.VIN, U3.OUT+, C1.+
  N16: M2.Vin-, U3.IN+, U4.IN+, U2.IN+
  N17: M2.Vin+, U5.P
  N18: TP1.pin3, U5.S, VCC1.+
  N19: TP1.pin6, U3.IN-, U4.IN-, U2.IN-, VCC1.-
  VCC_2: U4.OUT+, J7.Vcc, J8.Vcc, J9.Vcc, J10.Vcc, J11.Vcc, J12.Vcc
  GND_2: U4.OUT-, J7.gnd, J8.gnd, J9.gnd, J10.gnd, J11.gnd, J12.gnd
  GND_3: J1.gnd, J2.gnd, J3.gnd, J4.gnd, J5.gnd, J6.gnd, U2.OUT-
  VCC_3: J1.Vcc, J2.Vcc, J3.Vcc, J4.Vcc, J5.Vcc, J6.Vcc, U2.OUT+

custom parts:
  DOIT Esp32 DevKit v1 (30 pins long, 11 pins width): The DOIT Esp32 DevKit v1 is one of the development board created by DOIT to evaluate the ESP-WROOM-32 module. It is based on the ESP32 microcontroller that boasts Wifi, Bluetooth, Ethernet and Low Power support all in a single chip. (vanepp) made breadboard work, adjusted pin numbering and labels and reduced size of schematic and cleaned up pcb. This chip is 30pins long (2 x15) and 11 pins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
  INA219 DC Current Monitor Module: INA219 DC Current Monitor Module Links: INA219 product information
  TP4056: A DIP stand-in part for whatever IC you want. With 6 pins on a 300mil dual inline package (DIP) footprint.
  Mini-360 DC-DC Buck converter: Mini-360 DC-DC Buck converter. Tiny buck step down voltage converter, input voltage 4.75 to 23V output 1 to 17V adjustable. Available from ebay and the like.
